// Logisim project proj_2_1_top_solution.circ as structural Verilog: 6 circuits, main circuit testbench
module TOP (
  input  clk,
  input  rst,
  input  [31:0] inst,
  input  [31:0] memReadData,
  output [31:0] PC,
  output memWriteEnable,
  output [31:0] memWriteData,
  output [31:0] memAddress,
  output regWriteEnable,
  output [4:0] regWriteAddress,
  output [31:0] regWriteData,
  output memByteEnable3,
  output memByteEnable2,
  output memByteEnable1,
  output memByteEnable0
);

  wire ALUSrcA, ALUSrcB, ByteEnable0, ByteEnable1, ByteEnable2, ByteEnable3, Less, LSrc, memByteEnable0_t,
       memByteEnable1_t, memByteEnable2_t, memByteEnable3_t, memWriteEnable_t, regWriteEnable_t, SSrc, Zero;
  wire [1:0] PCSrc, ResultSrc;
  wire [2:0] ImmSrc;
  wire [3:0] ALUControl;
  wire [4:0] bit_extender_1_out, multiplier_1_out;
  wire [7:0] multiplexer_15_out;
  wire [31:0] ALUResult, bit_extender_2_out, bit_extender_3_out, imm, memWriteData_t, multiplexer_2_out,
       multiplexer_14_out, PC_t, PCNext, PCPlus4, PCTarget, ReadData, registerfile_1_rd1, regWriteData_t,
       shifter_1_out, WriteData;

  Register #(.width(32)) pcReg (.D(PCNext), .clk(clk), .Q(PC_t), .clr(rst));  // open: en
  Adder #(.width(32)) adder_1 (.a(PC_t), .b(32'h4), .out(PCPlus4));  // open: cin, cout
  Adder #(.width(32)) adder_2 (.a(PC_t), .b(imm), .out(PCTarget));  // open: cin, cout
  Multiplexer #(.select(2), .width(32)) multiplexer_1 (
    .in0(PCPlus4), .in1(PCTarget), .in2(ALUResult), .out(PCNext), .sel(PCSrc));  // open: in3
  Decoder #(.enable("false"), .select(2)) decoder_1 (
    .out0(ByteEnable0), .out1(ByteEnable1), .out2(ByteEnable2), .out3(ByteEnable3), .sel(ALUResult[1:0]));
  or or_1 (memByteEnable3_t, ByteEnable3, ~SSrc);  // OR_Gate
  or or_2 (memByteEnable2_t, ByteEnable2, ~SSrc);  // OR_Gate
  or or_3 (memByteEnable1_t, ByteEnable1, ~SSrc);  // OR_Gate
  or or_4 (memByteEnable0_t, ByteEnable0, ~SSrc);  // OR_Gate
  RegisterFile registerfile_1 (
    .CLK(clk), .A1(inst[19:15]), .A2(inst[24:20]), .A3(inst[11:7]), .WD3(regWriteData_t),
    .WE(regWriteEnable_t), .rst(rst), .RD1(registerfile_1_rd1), .RD2(WriteData));
  ControlUnit controlunit_1 (
    .opcode(inst[6:0]), .Funct3(inst[14:12]), .Funct7(inst[31:25]), .Zero(Zero), .Less(Less),
    .ResultSrc(ResultSrc), .MemWrite(memWriteEnable_t), .ALUControl(ALUControl), .ALUSrcA(ALUSrcA),
    .ALUSrcB(ALUSrcB), .ImmSrc(ImmSrc), .Regwrite(regWriteEnable_t), .PCSrc(PCSrc), .LSrc(LSrc), .SSrc(SSrc));
  Multiplexer #(.width(32)) multiplexer_2 (.in0(WriteData), .in1(imm), .out(multiplexer_2_out), .sel(ALUSrcB));
  Multiplexer #(.width(32)) multiplexer_3 (.in0(PC_t), .in1({32{1'b0}}), .out(PC), .sel(rst));
  Multiplexer multiplexer_4 (.in0(memWriteEnable_t), .in1(1'b0), .out(memWriteEnable), .sel(rst));
  Multiplexer #(.width(32)) multiplexer_5 (.in0(memWriteData_t), .in1({32{1'b0}}), .out(memWriteData), .sel(rst));
  Multiplexer #(.width(32)) multiplexer_6 (.in0(ALUResult), .in1({32{1'b0}}), .out(memAddress), .sel(rst));
  Multiplexer multiplexer_7 (.in0(regWriteEnable_t), .in1(1'b0), .out(regWriteEnable), .sel(rst));
  Multiplexer #(.width(5)) multiplexer_8 (.in0(inst[11:7]), .in1({5{1'b0}}), .out(regWriteAddress), .sel(rst));
  Multiplexer #(.width(32)) multiplexer_9 (.in0(regWriteData_t), .in1({32{1'b0}}), .out(regWriteData), .sel(rst));
  Multiplexer multiplexer_10 (.in0(memByteEnable3_t), .in1(1'b0), .out(memByteEnable3), .sel(rst));
  Multiplexer multiplexer_11 (.in0(memByteEnable2_t), .in1(1'b0), .out(memByteEnable2), .sel(rst));
  Multiplexer multiplexer_12 (.in0(memByteEnable1_t), .in1(1'b0), .out(memByteEnable1), .sel(rst));
  Multiplexer multiplexer_13 (.in0(memByteEnable0_t), .in1(1'b0), .out(memByteEnable0), .sel(rst));
  Multiplexer #(.width(32)) multiplexer_14 (
    .in0(registerfile_1_rd1), .in1({32{1'b0}}), .out(multiplexer_14_out), .sel(ALUSrcA));
  assign bit_extender_1_out = {{3{1'b0}}, ALUResult[1:0]};  // Bit_Extender bit_extender_1
  Multiplier #(.width(5)) multiplier_1 (
    .a(bit_extender_1_out), .b(5'b01000), .out(multiplier_1_out));  // open: cin, cout
  Multiplexer #(.select(2), .width(8)) multiplexer_15 (
    .in0(memReadData[7:0]), .in1(memReadData[15:8]), .in2(memReadData[23:16]), .in3(memReadData[31:24]),
    .out(multiplexer_15_out), .sel(ALUResult[1:0]));
  assign bit_extender_2_out = {{24{1'b0}}, WriteData[7:0]};  // Bit_Extender bit_extender_2
  assign bit_extender_3_out = {{24{multiplexer_15_out[7]}}, multiplexer_15_out};  // Bit_Extender bit_extender_3
  Shifter #(.width(32)) shifter_1 (.in(bit_extender_2_out), .\dist (multiplier_1_out), .out(shifter_1_out));
  Multiplexer #(.width(32)) multiplexer_16 (.in0(memReadData), .in1(bit_extender_3_out), .out(ReadData), .sel(LSrc));
  ALU alu_1 (
    .SrcA(multiplexer_14_out), .SrcB(multiplexer_2_out), .ALUControl(ALUControl), .ALUResult(ALUResult),
    .Zero(Zero), .Less(Less));
  Extend extend_1 (.ximm(inst[31:7]), .ImmSrc(ImmSrc), .ImmExt(imm));
  Multiplexer #(.width(32)) multiplexer_17 (.in0(WriteData), .in1(shifter_1_out), .out(memWriteData_t), .sel(SSrc));
  Multiplexer #(.select(2), .width(32)) multiplexer_18 (
    .in0(ALUResult), .in1(ReadData), .in2(PCPlus4), .in3(PCTarget), .out(regWriteData_t), .sel(ResultSrc));

  // Other names for the same wires on the sheet: regWriteAddress_t[4:0] = inst[11:7];
  //   memAddress1_0[1:0] = ALUResult[1:0]; memAddress_t[31:0] = ALUResult

  // Notes on the sheet:
  //   DON'T TOUCH!
endmodule

module testbench (
  input  rst,
  output [6:0] count,
  output [31:0] PC,
  output [31:0] memReadData,
  output halt,
  output [31:0] memAddress,
  output memWriteEnable,
  output [31:0] memWriteData,
  output memByteEnable3,
  output memByteEnable2,
  output memByteEnable1,
  output memByteEnable0,
  output regWriteEnable,
  output [4:0] regWriteAddress,
  output [31:0] regWriteData
);

  wire and_1_out, carry, clk, not_1_out, not_2_out, por_1_out, rst_t;
  wire [31:0] inst;

  not not_1 (not_1_out, inst[2]);
  not not_2 (not_2_out, inst[3]);
  POR por_1 (.out(por_1_out));
  TOP top_1 (
    .clk(clk), .rst(rst_t), .inst(inst), .memReadData(memReadData), .PC(PC), .memWriteEnable(memWriteEnable),
    .memWriteData(memWriteData), .memAddress(memAddress), .regWriteEnable(regWriteEnable),
    .regWriteAddress(regWriteAddress), .regWriteData(regWriteData), .memByteEnable3(memByteEnable3),
    .memByteEnable2(memByteEnable2), .memByteEnable1(memByteEnable1), .memByteEnable0(memByteEnable0));
  Clock clock_1 (.out(clk));
  or or_1 (rst_t, rst, por_1_out);
  and and_1 (and_1_out, inst[0], inst[1], not_1_out, not_2_out, inst[4], inst[5], inst[6]);
  or or_2 (halt, and_1_out, carry);
  Counter #(.max('h7f), .width(7)) counter_1 (
    .clr(rst_t), .up(1'b1), .count(1'b1), .clk(clk), .carry(carry), .Q(count));  // open: load, D
  // Probe on PC
  // Probe on PC[9:2]
  ROM #(.dataWidth(32), .misaligned("true")) rom_1 (.addr(PC[9:2]), .data(inst));
  // Probe on inst
  RAM #(.asyncread("true"), .byteenables("byteEnables"), .dataWidth(32)) ram_1 (
    .addr(memAddress[9:2]), .we(memWriteEnable), .clk(clk), .din(memWriteData), .dout(memReadData),
    .be3(memByteEnable3), .be2(memByteEnable2), .be1(memByteEnable1), .be0(memByteEnable0));  // open: oe

  // Notes on the sheet:
  //   DON'T TOUCH!
  //   contents of rom_1 (hex, n*v repeats v):
  //   20000db7 03300913 00500993 00100493 00700a13 ff900a93 ccccfb37 effb0b13 00000297 005da023 004d8d93
  //   014282e7 00000293 005da023 004d8d93 008002ef 00000293 005da023 004d8d93 016da023 000d8d13 004d8d93
  //   000d81a3 000d8123 000d8023 016d80a3 004d8d93 000d2283 005da023 004d8d93 000d0283 005da023 004d8d93
  //   013902b3 005da023 004d8d93 413902b3 005da023 004d8d93 013972b3 005da023 004d8d93 0144a2b3 005da023
  //   004d8d93 ff690293 005da023 004d8d93 0039f293 005da023 004d8d93 0004a293 005da023 004d8d93 00100293
  //   014a8463 00000293 005da023 004d8d93 00100293 014ac463 00000293 005da023 004d8d93 00000013 00000013
  //   00100073
  //   you can write any instruction in
  //   D_MEM
endmodule

module RegisterFile (
  input  CLK,
  input  [4:0] A1,
  input  [4:0] A2,
  input  [4:0] A3,
  input  [31:0] WD3,
  input  WE,
  input  rst,
  output [31:0] RD1,
  output [31:0] RD2
);

  wire enable0, enable8, enable16, enable24;
  wire [7:1] enable0_7, enable8_15, enable16_23, enable24_31;
  wire [31:0] decoder_1_out0, xrs1, xrs2, xrs3, xrs4, xrs5, xrs6, xrs7, xrs8, xrs9, xrs10, xrs11, xrs12,
       xrs13, xrs14, xrs15, xrs16, xrs17, xrs18, xrs19, xrs20, xrs21, xrs22, xrs23, xrs24, xrs25, xrs26,
       xrs27, xrs28, xrs29, xrs30, xrs31;

  Decoder #(.select(5)) decoder_1 (
    .out0(decoder_1_out0[0]), .out1(decoder_1_out0[1]), .out2(decoder_1_out0[2]), .out3(decoder_1_out0[3]),
    .out4(decoder_1_out0[4]), .out5(decoder_1_out0[5]), .out6(decoder_1_out0[6]), .out7(decoder_1_out0[7]),
    .out8(decoder_1_out0[8]), .out9(decoder_1_out0[9]), .out10(decoder_1_out0[10]),
    .out11(decoder_1_out0[11]), .out12(decoder_1_out0[12]), .out13(decoder_1_out0[13]),
    .out14(decoder_1_out0[14]), .out15(decoder_1_out0[15]), .out16(decoder_1_out0[16]),
    .out17(decoder_1_out0[17]), .out18(decoder_1_out0[18]), .out19(decoder_1_out0[19]),
    .out20(decoder_1_out0[20]), .out21(decoder_1_out0[21]), .out22(decoder_1_out0[22]),
    .out23(decoder_1_out0[23]), .out24(decoder_1_out0[24]), .out25(decoder_1_out0[25]),
    .out26(decoder_1_out0[26]), .out27(decoder_1_out0[27]), .out28(decoder_1_out0[28]),
    .out29(decoder_1_out0[29]), .out30(decoder_1_out0[30]), .out31(decoder_1_out0[31]), .sel(A3), .en(WE));
  Multiplexer #(.width(32)) multiplexer_1 (
    .in0(decoder_1_out0), .in1({32{1'b0}}),
    .out({enable24_31, enable24, enable16_23, enable16, enable8_15, enable8, enable0_7, enable0}), .sel(rst));
  Register #(.width(32)) register_1 (.D(WD3), .en(enable0_7[1]), .clk(CLK), .Q(xrs1), .clr(rst));
  Register #(.width(32)) register_2 (.D(WD3), .en(enable0_7[2]), .clk(CLK), .Q(xrs2), .clr(rst));
  Register #(.width(32)) register_3 (.D(WD3), .en(enable0_7[3]), .clk(CLK), .Q(xrs3), .clr(rst));
  Register #(.width(32)) register_4 (.D(WD3), .en(enable0_7[4]), .clk(CLK), .Q(xrs4), .clr(rst));
  Register #(.width(32)) register_5 (.D(WD3), .en(enable0_7[5]), .clk(CLK), .Q(xrs5), .clr(rst));
  Register #(.width(32)) register_6 (.D(WD3), .en(enable0_7[6]), .clk(CLK), .Q(xrs6));  // open: clr
  Register #(.width(32)) register_7 (.D(WD3), .en(enable0_7[7]), .clk(CLK), .Q(xrs7), .clr(rst));
  Register #(.width(32)) register_8 (.D(WD3), .en(enable8), .clk(CLK), .Q(xrs8), .clr(rst));
  Register #(.width(32)) register_9 (.D(WD3), .en(enable8_15[1]), .clk(CLK), .Q(xrs9), .clr(rst));
  Register #(.width(32)) register_10 (.D(WD3), .en(enable8_15[2]), .clk(CLK), .Q(xrs10), .clr(rst));
  Register #(.width(32)) register_11 (.D(WD3), .en(enable8_15[3]), .clk(CLK), .Q(xrs11), .clr(rst));
  Register #(.width(32)) register_12 (.D(WD3), .en(enable8_15[4]), .clk(CLK), .Q(xrs12), .clr(rst));
  Register #(.width(32)) register_13 (.D(WD3), .en(enable8_15[5]), .clk(CLK), .Q(xrs13), .clr(rst));
  Register #(.width(32)) register_14 (.D(WD3), .en(enable8_15[6]), .clk(CLK), .Q(xrs14));  // open: clr
  Register #(.width(32)) register_15 (.D(WD3), .en(enable8_15[7]), .clk(CLK), .Q(xrs15), .clr(rst));
  Multiplexer #(.select(5), .width(32)) multiplexer_2 (
    .in0({32{1'b0}}), .in1(xrs1), .in2(xrs2), .in3(xrs3), .in4(xrs4), .in5(xrs5), .in6(xrs6), .in7(xrs7),
    .in8(xrs8), .in9(xrs9), .in10(xrs10), .in11(xrs11), .in12(xrs12), .in13(xrs13), .in14(xrs14),
    .in15(xrs15), .in16(xrs16), .in17(xrs17), .in18(xrs18), .in19(xrs19), .in20(xrs20), .in21(xrs21),
    .in22(xrs22), .in23(xrs23), .in24(xrs24), .in25(xrs25), .in26(xrs26), .in27(xrs27), .in28(xrs28),
    .in29(xrs29), .in30(xrs30), .in31(xrs31), .out(RD1), .sel(A1));
  Register #(.width(32)) register_16 (.D(WD3), .en(enable16), .clk(CLK), .Q(xrs16), .clr(rst));
  Register #(.width(32)) register_17 (.D(WD3), .en(enable16_23[1]), .clk(CLK), .Q(xrs17), .clr(rst));
  Register #(.width(32)) register_18 (.D(WD3), .en(enable16_23[2]), .clk(CLK), .Q(xrs18), .clr(rst));
  Register #(.width(32)) register_19 (.D(WD3), .en(enable16_23[3]), .clk(CLK), .Q(xrs19), .clr(rst));
  Register #(.width(32)) register_20 (.D(WD3), .en(enable16_23[4]), .clk(CLK), .Q(xrs20), .clr(rst));
  Register #(.width(32)) register_21 (.D(WD3), .en(enable16_23[5]), .clk(CLK), .Q(xrs21), .clr(rst));
  Register #(.width(32)) register_22 (.D(WD3), .en(enable16_23[6]), .clk(CLK), .Q(xrs22));  // open: clr
  Register #(.width(32)) register_23 (.D(WD3), .en(enable16_23[7]), .clk(CLK), .Q(xrs23), .clr(rst));
  Multiplexer #(.select(5), .width(32)) multiplexer_3 (
    .in0({32{1'b0}}), .in1(xrs1), .in2(xrs2), .in3(xrs3), .in4(xrs4), .in5(xrs5), .in6(xrs6), .in7(xrs7),
    .in8(xrs8), .in9(xrs9), .in10(xrs10), .in11(xrs11), .in12(xrs12), .in13(xrs13), .in14(xrs14),
    .in15(xrs15), .in16(xrs16), .in17(xrs17), .in18(xrs18), .in19(xrs19), .in20(xrs20), .in21(xrs21),
    .in22(xrs22), .in23(xrs23), .in24(xrs24), .in25(xrs25), .in26(xrs26), .in27(xrs27), .in28(xrs28),
    .in29(xrs29), .in30(xrs30), .in31(xrs31), .out(RD2), .sel(A2));
  Register #(.width(32)) register_24 (.D(WD3), .en(enable24), .clk(CLK), .Q(xrs24), .clr(rst));
  Register #(.width(32)) register_25 (.D(WD3), .en(enable24_31[1]), .clk(CLK), .Q(xrs25), .clr(rst));
  Register #(.width(32)) register_26 (.D(WD3), .en(enable24_31[2]), .clk(CLK), .Q(xrs26), .clr(rst));
  Register #(.width(32)) register_27 (.D(WD3), .en(enable24_31[3]), .clk(CLK), .Q(xrs27), .clr(rst));
  Register #(.width(32)) register_28 (.D(WD3), .en(enable24_31[4]), .clk(CLK), .Q(xrs28), .clr(rst));
  Register #(.width(32)) register_29 (.D(WD3), .en(enable24_31[5]), .clk(CLK), .Q(xrs29), .clr(rst));
  Register #(.width(32)) register_30 (.D(WD3), .en(enable24_31[6]), .clk(CLK), .Q(xrs30), .clr(rst));
  Register #(.width(32)) register_31 (.D(WD3), .en(enable24_31[7]), .clk(CLK), .Q(xrs31), .clr(rst));

  // Other names for the same wires on the sheet: enable0_7[0] = enable0; enable1 = enable0_7[1];
  //   enable2 = enable0_7[2]; enable3 = enable0_7[3]; enable4 = enable0_7[4]; enable5 = enable0_7[5];
  //   enable6 = enable0_7[6]; enable7 = enable0_7[7]; enable8_15[0] = enable8; enable9 = enable8_15[1];
  //   enable10 = enable8_15[2]; enable11 = enable8_15[3]; enable12 = enable8_15[4]; enable13 = enable8_15[5];
  //   enable14 = enable8_15[6]; enable15 = enable8_15[7]; enable16_23[0] = enable16; enable17 = enable16_23[1];
  //   enable18 = enable16_23[2]; enable19 = enable16_23[3]; enable20 = enable16_23[4]; enable21 = enable16_23[5];
  //   enable22 = enable16_23[6]; enable23 = enable16_23[7]; enable24_31[0] = enable24; enable25 = enable24_31[1];
  //   enable26 = enable24_31[2]; enable27 = enable24_31[3]; enable28 = enable24_31[4]; enable29 = enable24_31[5];
  //   enable30 = enable24_31[6]; enable31 = enable24_31[7]; rd[4:0] = A3; rs1[4:0] = A1; rs2[4:0] = A2;
  //   xrd[31:0] = WD3
endmodule

module ControlUnit (
  input  [6:0] opcode,
  input  [2:0] Funct3,
  input  [6:0] Funct7,
  input  Zero,
  input  Less,
  output [1:0] ResultSrc,
  output MemWrite,
  output [3:0] ALUControl,
  output ALUSrcA,
  output ALUSrcB,
  output [2:0] ImmSrc,
  output Regwrite,
  output [1:0] PCSrc,
  output LSrc,
  output SSrc
);

  wire and_4_out, and_5_out, and_8_out, B_Type, BVaild, comparator_10_eq, comparator_11_eq, comparator_12_eq,
       comparator_13_eq, I1_Type, I_Type_imm, I_Type_jalr, I_Type_Load, J_Type, or_4_out, or_5_out, or_6_out,
       priority_encoder_1_en_out, priority_encoder_2_en_out, priority_encoder_3_en_out, R_Type, U_Type,
       U_Type_auipc;
  wire [1:0] priority_encoder_1_out, priority_encoder_2_out;
  wire [2:0] priority_encoder_3_out;
  wire [3:0] ALU_Sel_B, ALU_Sel_I, ALU_Sel_R, bit_extender_1_out, bit_extender_2_out, bit_extender_3_out,
       I2ALUSel_data, R2ALUSel_data;

  ROM #(.addrWidth(3), .dataWidth(4)) I2ALUSel (.addr(Funct3), .data(I2ALUSel_data));
  assign bit_extender_1_out = {{3{B_Type}}, B_Type};  // Bit_Extender bit_extender_1
  Comparator #(.mode("unsigned"), .width(7)) comparator_1 (.a(opcode), .b(7'b0110011), .eq(R_Type));  // open: gt, lt
  Comparator #(.mode("unsigned"), .width(7)) comparator_2 (
    .a(opcode), .b(7'b0010011), .eq(I_Type_imm));  // open: gt, lt
  Comparator #(.mode("unsigned"), .width(7)) comparator_3 (
    .a(opcode), .b(7'b0000011), .eq(I_Type_Load));  // open: gt, lt
  Comparator #(.mode("unsigned"), .width(7)) comparator_4 (.a(opcode), .b(7'b0100011), .eq(MemWrite));  // open: gt, lt
  Comparator #(.mode("unsigned"), .width(7)) comparator_5 (.a(opcode), .b(7'b0110111), .eq(ALUSrcA));  // open: gt, lt
  Comparator #(.mode("unsigned"), .width(7)) comparator_6 (
    .a(opcode), .b(7'b0010111), .eq(U_Type_auipc));  // open: gt, lt
  Comparator #(.mode("unsigned"), .width(7)) comparator_7 (.a(opcode), .b(7'b1101111), .eq(J_Type));  // open: gt, lt
  Comparator #(.mode("unsigned"), .width(7)) comparator_8 (.a(opcode), .b(7'b1100011), .eq(B_Type));  // open: gt, lt
  Comparator #(.mode("unsigned"), .width(7)) comparator_9 (
    .a(opcode), .b(7'b1100111), .eq(I_Type_jalr));  // open: gt, lt
  ROM #(.addrWidth(4), .dataWidth(4)) R2ALUSel (.addr({Funct3, Funct7[5]}), .data(R2ALUSel_data));
  Comparator #(.mode("unsigned"), .width(3)) comparator_10 (
    .a(Funct3), .b(3'b000), .eq(comparator_10_eq));  // open: gt, lt
  Comparator #(.mode("unsigned"), .width(3)) comparator_11 (
    .a(Funct3), .b(3'b000), .eq(comparator_11_eq));  // open: gt, lt
  Comparator #(.mode("unsigned"), .width(3)) comparator_12 (
    .a(Funct3), .b(3'b000), .eq(comparator_12_eq));  // open: gt, lt
  Comparator #(.mode("unsigned"), .width(3)) comparator_13 (
    .a(Funct3), .b(3'b100), .eq(comparator_13_eq));  // open: gt, lt
  assign ALU_Sel_B = bit_extender_1_out & 4'b0001;  // AND_Gate and_1, 4 bits wide
  and and_2 (LSrc, comparator_10_eq, I_Type_Load);
  and and_3 (SSrc, comparator_11_eq, MemWrite);
  and and_4 (and_4_out, comparator_12_eq, Zero);
  and and_5 (and_5_out, comparator_13_eq, Less);
  assign bit_extender_2_out = {{3{I_Type_imm}}, I_Type_imm};  // Bit_Extender bit_extender_2
  assign bit_extender_3_out = {{3{R_Type}}, R_Type};  // Bit_Extender bit_extender_3
  assign ALU_Sel_I = bit_extender_2_out & I2ALUSel_data;  // AND_Gate and_6, 4 bits wide
  or or_1 (BVaild, and_4_out, and_5_out);
  assign ALU_Sel_R = bit_extender_3_out & R2ALUSel_data;  // AND_Gate and_7, 4 bits wide
  or or_2 (I1_Type, I_Type_imm, I_Type_Load, I_Type_jalr);
  or or_3 (U_Type, ALUSrcA, U_Type_auipc);
  or or_4 (or_4_out, R_Type, I_Type_imm, ALUSrcA);
  or or_5 (or_5_out, J_Type, I_Type_jalr);
  and and_8 (and_8_out, BVaild, B_Type);
  or or_6 (or_6_out, and_8_out, J_Type);
  or or_7 (Regwrite, R_Type, I1_Type, J_Type, U_Type);
  Priority_Encoder #(.select(2)) priority_encoder_1 (
    .in1(or_6_out), .in2(I_Type_jalr), .out(priority_encoder_1_out), .en_out(priority_encoder_1_en_out));  // open: in0, in3, gs, en_in
  Priority_Encoder #(.select(2)) priority_encoder_2 (
    .in0(or_4_out), .in1(I_Type_Load), .in2(or_5_out), .in3(U_Type_auipc), .out(priority_encoder_2_out),
    .en_out(priority_encoder_2_en_out));  // open: gs, en_in
  or or_8 (ALUSrcB, I1_Type, MemWrite, U_Type);
  Priority_Encoder priority_encoder_3 (
    .in0(I1_Type), .in1(MemWrite), .in2(B_Type), .in3(J_Type), .in5(U_Type), .out(priority_encoder_3_out),
    .en_out(priority_encoder_3_en_out));  // open: in4, in6, in7, en_in, gs
  assign ALUControl = ALU_Sel_R | ALU_Sel_B | ALU_Sel_I;  // OR_Gate or_9, 4 bits wide
  Multiplexer #(.width(3)) multiplexer_1 (
    .in0(priority_encoder_3_out), .in1(3'b000), .out(ImmSrc), .sel(priority_encoder_3_en_out));
  Multiplexer #(.width(2)) multiplexer_2 (
    .in0(priority_encoder_1_out), .in1(2'b00), .out(PCSrc), .sel(priority_encoder_1_en_out));
  Multiplexer #(.width(2)) multiplexer_3 (
    .in0(priority_encoder_2_out), .in1(2'b00), .out(ResultSrc), .sel(priority_encoder_2_en_out));

  // Other names for the same wires on the sheet: Funct7_Activate = Funct7[5]; S_Type = MemWrite; U_Type_lui = ALUSrcA

  // Notes on the sheet:
  //   beq
  //   blt
  //   contents of I2ALUSel (hex, n*v repeats v):
  //   0 2 3 4 5 6 8 9
  //   contents of R2ALUSel (hex, n*v repeats v):
  //   0 1 2 f 3 f 4 f 5 f 6 7 8 f 9 f
  //   R-Type Decoder
  //   I-Type Decoder
  //   L-Type Decoder
  //   S-Type Decoder
  //   B-Type Decoder
endmodule

module ALU (
  input  [31:0] SrcA,
  input  [31:0] SrcB,
  input  [3:0] ALUControl,
  output [31:0] ALUResult,
  output Zero,
  output Less
);

  wire comparator_2_lt, comparator_3_lt;
  wire [31:0] adder_1_out, and_1_out, bit_extender_1_out, bit_extender_2_out, or_1_out, shifter_1_out,
       shifter_2_out, shifter_3_out, subtractor_1_out, xor_1_out;

  Comparator #(.width(32)) comparator_1 (.a(ALUResult), .b({32{1'b0}}), .eq(Zero));  // open: gt, lt
  Adder #(.width(32)) adder_1 (.a(SrcA), .b(SrcB), .out(adder_1_out));  // open: cin, cout
  Subtractor #(.width(32)) subtractor_1 (.a(SrcA), .b(SrcB), .out(subtractor_1_out));  // open: bin, bout
  Shifter #(.width(32)) shifter_1 (.in(SrcA), .\dist (SrcB[4:0]), .out(shifter_1_out));
  Comparator #(.width(32)) comparator_2 (.a(SrcA), .b(SrcB), .lt(comparator_2_lt));  // open: gt, eq
  Comparator #(.mode("unsigned"), .width(32)) comparator_3 (.a(SrcA), .b(SrcB), .lt(comparator_3_lt));  // open: gt, eq
  assign xor_1_out = SrcA ^ SrcB;  // XOR_Gate xor_1, 32 bits wide
  Shifter #(.shift("lr"), .width(32)) shifter_2 (.in(SrcA), .\dist (SrcB[4:0]), .out(shifter_2_out));
  Shifter #(.shift("ar"), .width(32)) shifter_3 (.in(SrcA), .\dist (SrcB[4:0]), .out(shifter_3_out));
  assign or_1_out = SrcA | SrcB;  // OR_Gate or_1, 32 bits wide
  assign and_1_out = SrcA & SrcB;  // AND_Gate and_1, 32 bits wide
  assign bit_extender_1_out = {{31{1'b0}}, comparator_2_lt};  // Bit_Extender bit_extender_1
  assign bit_extender_2_out = {{31{1'b0}}, comparator_3_lt};  // Bit_Extender bit_extender_2
  Multiplexer #(.select(4), .width(32)) multiplexer_1 (
    .in0(adder_1_out), .in1(subtractor_1_out), .in2(shifter_1_out), .in3(bit_extender_1_out),
    .in4(bit_extender_2_out), .in5(xor_1_out), .in6(shifter_2_out), .in7(shifter_3_out), .in8(or_1_out),
    .in9(and_1_out), .out(ALUResult), .sel(ALUControl));  // open: in10, in11, in12, in13, in14, in15

  assign Less = ALUResult[31];

  // Other names for the same wires on the sheet: Result[31:0] = ALUResult

  // Notes on the sheet:
  //   I/O
endmodule

module Extend (
  input  [24:0] ximm,
  input  [2:0] ImmSrc,
  output [31:0] ImmExt
);

  wire [11:0] bit_extender_4_out;
  wire [19:0] bit_extender_3_out;
  wire [20:0] bit_extender_1_out, bit_extender_2_out;
  wire [31:0] bit_extender_5_out;

  assign bit_extender_1_out = {{20{ximm[24]}}, ximm[24]};  // Bit_Extender bit_extender_1
  assign bit_extender_2_out = {{20{ximm[24]}}, ximm[24]};  // Bit_Extender bit_extender_2
  assign bit_extender_3_out = {{19{ximm[24]}}, ximm[24]};  // Bit_Extender bit_extender_3
  assign bit_extender_4_out = {{11{ximm[24]}}, ximm[24]};  // Bit_Extender bit_extender_4
  assign bit_extender_5_out = {{27{1'b0}}, ximm[17:13]};  // Bit_Extender bit_extender_5
  Multiplexer #(.select(3), .width(32)) multiplexer_1 (
    .in0({bit_extender_1_out, ximm[23:13]}), .in1({bit_extender_2_out, ximm[23:18], ximm[4:0]}),
    .in2({bit_extender_3_out, ximm[0], ximm[23:18], ximm[4:1], 1'b0}),
    .in3({bit_extender_4_out, ximm[12:5], ximm[13], ximm[23:14], 1'b0}), .in4(bit_extender_5_out),
    .in5({ximm[24:5], {12{1'b0}}}), .out(ImmExt), .sel(ImmSrc));  // open: in6, in7

  // Notes on the sheet:
  //   I1
  //   S
  //   B
  //   J
  //   I2
  //   U
endmodule
