// Logisim project proj_2_2_top.circ as structural Verilog: 2 circuits, main circuit testbench
module TOP (
  input  clk,
  input  rst,
  input  [31:0] inst,
  input  [31:0] memReadData,
  output [31:0] PC,
  output memWriteEnable,
  output [31:0] memWriteData,
  output [31:0] memAddress,
  output regWriteEnable,
  output [4:0] regWriteAddress,
  output [31:0] regWriteData,
  output memByteEnable3,
  output memByteEnable2,
  output memByteEnable1,
  output memByteEnable0
);

  wire memByteEnable0_t, memByteEnable1_t, memByteEnable2_t, memByteEnable3_t, memWriteEnable_t,
       regWriteEnable_t;
  wire [4:0] regWriteAddress_t;
  wire [31:0] memAddress_t, memWriteData_t, PC_t, regWriteData_t;

  Multiplexer #(.width(32)) multiplexer_1 (.in0(PC_t), .in1({32{1'b0}}), .out(PC), .sel(rst));
  Multiplexer multiplexer_2 (.in0(memWriteEnable_t), .in1(1'b0), .out(memWriteEnable), .sel(rst));
  Multiplexer #(.width(32)) multiplexer_3 (.in0(memWriteData_t), .in1({32{1'b0}}), .out(memWriteData), .sel(rst));
  Multiplexer #(.width(32)) multiplexer_4 (.in0(memAddress_t), .in1({32{1'b0}}), .out(memAddress), .sel(rst));
  Multiplexer multiplexer_5 (.in0(regWriteEnable_t), .in1(1'b0), .out(regWriteEnable), .sel(rst));
  Multiplexer #(.width(5)) multiplexer_6 (.in0(regWriteAddress_t), .in1({5{1'b0}}), .out(regWriteAddress), .sel(rst));
  Multiplexer #(.width(32)) multiplexer_7 (.in0(regWriteData_t), .in1({32{1'b0}}), .out(regWriteData), .sel(rst));
  Multiplexer multiplexer_8 (.in0(memByteEnable3_t), .in1(1'b0), .out(memByteEnable3), .sel(rst));
  Multiplexer multiplexer_9 (.in0(memByteEnable2_t), .in1(1'b0), .out(memByteEnable2), .sel(rst));
  Multiplexer multiplexer_10 (.in0(memByteEnable1_t), .in1(1'b0), .out(memByteEnable1), .sel(rst));
  Multiplexer multiplexer_11 (.in0(memByteEnable0_t), .in1(1'b0), .out(memByteEnable0), .sel(rst));

  // Notes on the sheet:
  //   DON'T TOUCH!
endmodule

module testbench (
  input  rst,
  output [6:0] count,
  output [31:0] PC,
  output [31:0] memReadData,
  output halt,
  output [31:0] memAddress,
  output memWriteEnable,
  output [31:0] memWriteData,
  output memByteEnable3,
  output memByteEnable2,
  output memByteEnable1,
  output memByteEnable0,
  output regWriteEnable,
  output [4:0] regWriteAddress,
  output [31:0] regWriteData
);

  wire and_1_out, carry, clk, not_1_out, not_2_out, por_1_out, rst_t;
  wire [31:0] inst;

  not not_1 (not_1_out, inst[2]);
  not not_2 (not_2_out, inst[3]);
  POR por_1 (.out(por_1_out));
  TOP top_1 (
    .clk(clk), .rst(rst_t), .inst(inst), .memReadData(memReadData), .PC(PC), .memWriteEnable(memWriteEnable),
    .memWriteData(memWriteData), .memAddress(memAddress), .regWriteEnable(regWriteEnable),
    .regWriteAddress(regWriteAddress), .regWriteData(regWriteData), .memByteEnable3(memByteEnable3),
    .memByteEnable2(memByteEnable2), .memByteEnable1(memByteEnable1), .memByteEnable0(memByteEnable0));
  Clock clock_1 (.out(clk));
  or or_1 (rst_t, rst, por_1_out);
  and and_1 (and_1_out, inst[0], inst[1], not_1_out, not_2_out, inst[4], inst[5], inst[6]);
  or or_2 (halt, and_1_out, carry);
  Counter #(.max('h7f), .width(7)) counter_1 (
    .clr(rst_t), .up(1'b1), .count(1'b1), .clk(clk), .carry(carry), .Q(count));  // open: load, D
  // Probe on PC
  // Probe on PC[9:2]
  ROM #(.dataWidth(32), .misaligned("true")) rom_1 (.addr(PC[9:2]), .data(inst));
  // Probe on inst
  RAM #(.asyncread("true"), .byteenables("byteEnables"), .dataWidth(32)) ram_1 (
    .addr(memAddress[9:2]), .we(memWriteEnable), .clk(clk), .din(memWriteData), .dout(memReadData),
    .be3(memByteEnable3), .be2(memByteEnable2), .be1(memByteEnable1), .be0(memByteEnable0));  // open: oe

  // Notes on the sheet:
  //   DON'T TOUCH!
  //   contents of rom_1 (hex, n*v repeats v):
  //   20000db7 03300913 00500993 00100493 00700a13 ff900a93 ccccfb37 effb0b13 00000297 005da023 004d8d93
  //   014282e7 00000293 005da023 004d8d93 008002ef 00000293 005da023 004d8d93 016da023 000d8d13 004d8d93
  //   000d81a3 000d8123 000d8023 016d80a3 004d8d93 000d2283 005da023 004d8d93 000d0283 005da023 004d8d93
  //   013902b3 005da023 004d8d93 413902b3 005da023 004d8d93 013972b3 005da023 004d8d93 0144a2b3 005da023
  //   004d8d93 ff690293 005da023 004d8d93 0039f293 005da023 004d8d93 0004a293 005da023 004d8d93 00100293
  //   014a8463 00000293 005da023 004d8d93 00100293 014ac463 00000293 005da023 004d8d93 00000013 00000013
  //   00100073
  //   you can write any instruction in
  //   D_MEM
endmodule
