// Logisim project p22_localtest.circ as structural Verilog: 1 circuit, main circuit main
module main (
  input  rst,
  output [6:0] count,
  output [31:0] PC,
  output [31:0] memReadData,
  output halt,
  output [31:0] memAddress,
  output memWriteEnable,
  output [31:0] memWriteData,
  output memByteEnable3,
  output memByteEnable2,
  output memByteEnable1,
  output memByteEnable0,
  output regWriteEnable,
  output [4:0] regWriteAddress,
  output [31:0] regWriteData
);

  wire and_1_out, carry, clk, not_1_out, not_2_out, por_1_out, rst_t;
  wire [31:0] inst;

  not not_1 (not_1_out, inst[2]);
  not not_2 (not_2_out, inst[3]);
  POR por_1 (.out(por_1_out));
  TOP top_1 (
    .clk(clk), .rst(rst_t), .inst(inst), .memReadData(memReadData), .PC(PC), .memWriteEnable(memWriteEnable),
    .memWriteData(memWriteData), .memAddress(memAddress), .regWriteEnable(regWriteEnable),
    .regWriteAddress(regWriteAddress), .regWriteData(regWriteData), .memByteEnable3(memByteEnable3),
    .memByteEnable2(memByteEnable2), .memByteEnable1(memByteEnable1), .memByteEnable0(memByteEnable0));
  Clock clock_1 (.out(clk));
  or or_1 (rst_t, rst, por_1_out);
  and and_1 (and_1_out, inst[0], inst[1], not_1_out, not_2_out, inst[4], inst[5], inst[6]);
  or or_2 (halt, and_1_out, carry);
  Counter #(.max('h7f), .width(7)) counter_1 (
    .clr(rst_t), .up(1'b1), .count(1'b1), .clk(clk), .carry(carry), .Q(count));  // open: load, D
  // Probe on PC
  // Probe on PC[9:2]
  ROM #(.dataWidth(32), .misaligned("true")) rom_1 (.addr(PC[9:2]), .data(inst));
  // Probe on inst
  RAM #(.asyncread("true"), .byteenables("byteEnables"), .dataWidth(32)) ram_1 (
    .addr(memAddress[9:2]), .we(memWriteEnable), .clk(clk), .din(memWriteData), .dout(memReadData),
    .be3(memByteEnable3), .be2(memByteEnable2), .be1(memByteEnable1), .be0(memByteEnable0));  // open: oe

  // Notes on the sheet:
  //   DON'T TOUCH!
  //   contents of rom_1 (hex, n*v repeats v):
  //   20000db7 03300913 00500993 00100493 00700a13 ff900a93 ccccfb37 effb0b13 00000297 005da023 004d8d93
  //   014282e7 00000293 005da023 004d8d93 008002ef 00000293 005da023 004d8d93 016da023 000d8d13 004d8d93
  //   000d81a3 000d8123 000d8023 016d80a3 004d8d93 000d2283 005da023 004d8d93 000d0283 005da023 004d8d93
  //   013902b3 005da023 004d8d93 413902b3 005da023 004d8d93 013972b3 005da023 004d8d93 0144a2b3 005da023
  //   004d8d93 ff690293 005da023 004d8d93 0039f293 005da023 004d8d93 0004a293 005da023 004d8d93 00100293
  //   014a8463 00000293 005da023 004d8d93 00100293 014ac463 00000293 005da023 004d8d93 00000013 00000013
  //   00100073
  //   you can write any instruction in
  //   D_MEM
endmodule
